# Fritzing sketch Reciever sketch (saved by Fritzing 0.8.7b)
breadboards: 1

parts:
  Part1 = Arduino Nano (Rev3.0)
  S1 = H-Bridge with L298N
  M1 = DC Motor
  M2 = DC Motor
  M3 = DC Motor
  M4 = DC Motor
  Transceiver1 = nRF24L01 [package=module]

nets:
  GND: Part1.GND, S1.GND, Transceiver1.GND
  N1: Part1.D2, S1.IN3
  N2: Part1.D3, S1.ENA
  N3: Part1.D4, S1.IN4
  N4: Part1.D5, S1.IN1
  N5: Part1.D6, S1.IN2
  N6: Part1.D7, Transceiver1.CE
  N7: Part1.D8, Transceiver1.CSN
  N8: Part1.D9, S1.ENB
  N9: Part1.D11/MOSI, Transceiver1.MOSI
  N10: Part1.D12/MISO, Transceiver1.MISO
  VIN: Part1.VIN, S1.5V
  3V3: Part1.3V3, Transceiver1.VCC
  N11: Part1.D13/SCK, Transceiver1.SCK
  N12: S1.M1-01, M3.pin_2, M4.pin_2
  N13: S1.M1-02, M3.pin_1, M4.pin_1
  N14: S1.M2-01, M1.pin_2, M2.pin_2
  N15: S1.M2-02, M1.pin_1, M2.pin_1

custom parts:
  H-Bridge with L298N: h-bridge
  nRF24L01: nRF24L01 module
