# Fritzing sketch Transmitter sketch (saved by Fritzing 0.8.7b)

parts:
  Part1 = Arduino Uno (Rev3)
  Part2 = Thumb Joystick
  Transceiver1 = nRF24L01 [package=module]

nets:
  N1: Part1.A0, Part2.HORZ
  N2: Part1.A1, Part2.VERT
  N3: Part1.D8, Transceiver1.CSN
  N4: Part1.D11_PWM/MOSI, Transceiver1.MOSI
  N5: Part1.D12/MISO, Transceiver1.MISO
  N6: Part1.D13/SCK, Transceiver1.SCK
  N7: Part1.D7, Transceiver1.CE
  3V3: Part1.3V3, Transceiver1.VCC
  5V: Part1.5V, Part2.VCC
  GND: Part1.GND, Part2.GND, Transceiver1.GND

custom parts:
  nRF24L01: nRF24L01 module
